# Fritzing sketch energy-consumption-monitor (saved by Fritzing 0.9.9b)

parts:
  J17 = female pin header, 2 pins [form="♀ (female)"]
  J18 = female pin header, 2 pins [form="♀ (female)"]
  J19 = female pin header, 2 pins [form="♀ (female)"]
  J20 = female pin header, 2 pins [form="♀ (female)"]
  J21 = female pin header, 2 pins [form="♀ (female)"]
  J22 = female pin header, 2 pins [form="♀ (female)"]
  GSM_SIM_GPSR_SMS_SIM900_SIM2 = SIM800L [package=THT]
  microSD2 = MicroSD Card Module
  ZS-042_RTC2 = ZS-042 RTC Module
  LCD2004-I2C2 = LCD2004-I2C
  Mod2 = zmpt101b
  Part4 = ACS712 Current Sensor 5A 20A 30A
  o2 = Module display OLED I2C 128x64 SSD1306 [package=THT]
  TP2 = TP4056 [chip_label=TP4056 package="DIP (Dual Inline) [THT]"]
  U3 = LIPO-110mAh [package=lipo-110]
  J23 = female pin header, 2 pins [form="♀ (female)"]
  J24 = female pin header, 2 pins [form="♀ (female)"]
  J25 = female pin header, 2 pins [form="♀ (female)"]
  J26 = female pin header, 2 pins [form="♀ (female)"]
  J29 = female pin header, 2 pins [form="♀ (female)"]
  J30 = female pin header, 2 pins [form="♀ (female)"]
  J31 = female pin header, 2 pins [form="♀ (female)"]
  J32 = female pin header, 2 pins [form="♀ (female)"]
  M2 = RioRand LM2596
  Part5 = Arduino Mega 2560 (Rev3)
  Part6 = Arduino Nano (Rev3.0)

nets:
  N1: J17.pin1, J19.pin1, Part4.VCC
  N2: J17.pin2, J19.pin2, Part4.GND
  N3: J18.pin1, Part4.2, Part4.OUT, Part5.A1
  N4: J18.pin2, Mod2.OUT, Part5.A0
  N5: J20.pin1, Mod2.GND, J29.pin1
  N6: J20.pin2, Mod2.VCC, J29.pin2
  GND: J21.pin1, J22.pin1, GSM_SIM_GPSR_SMS_SIM900_SIM2.GND#5, o2.GND, Part5.GND, Part6.GND
  N7: J21.pin2, J22.pin2, Part5.5V
  N8: GSM_SIM_GPSR_SMS_SIM900_SIM2.5V, J30.pin2
  N9: GSM_SIM_GPSR_SMS_SIM900_SIM2.GND#1, J30.pin1
  N10: GSM_SIM_GPSR_SMS_SIM900_SIM2.SIM_TXD, Part5.D6_PWM
  N11: GSM_SIM_GPSR_SMS_SIM900_SIM2.SIM_RXD, Part5.D5_PWM
  N12: microSD2.GND, J23.pin2
  N13: microSD2.VCC, J23.pin1
  N14: microSD2.MISO, Part5.D48
  N15: microSD2.MOSI, Part5.D49
  N16: microSD2.SCK, Part5.D50
  N17: microSD2.CS, Part5.D51
  N18: ZS-042_RTC2.GND, J25.pin2
  N19: ZS-042_RTC2.VCC, J25.pin1
  N20: ZS-042_RTC2.SDA, Part5.SDA
  N21: ZS-042_RTC2.SCL, Part5.SCL
  N22: LCD2004-I2C2.GND, J24.pin1
  N23: LCD2004-I2C2.VCC, J24.pin2
  N24: LCD2004-I2C2.SDA, J26.pin1
  N25: LCD2004-I2C2.SCL, J26.pin2
  VCC: o2.VCC, Part6.5V
  N26: o2.SCL, Part6.A5
  N27: o2.SDA, Part6.A4
  N28: TP2.pin1, J31.pin1
  N29: TP2.pin2, J31.pin2
  N30: TP2.pin3, M2.Pin_1
  N31: TP2.pin4, U3.+
  N32: TP2.pin5, U3.-
  N33: TP2.pin6, M2.Pin_2
  N34: J32.pin1, M2.Pin_3
  N35: J32.pin2, M2.Pin_4
  N36: Part5.D3_PWM, Part6.D0/RX

custom parts:
  LCD2004-I2C: A standard character display with 4x20 characters. Comes in many colors with LCM2004 IIC attached.
  zmpt101b: Single phase ac active output voltate transformer module.
  ACS712 Current Sensor 5A 20A 30A: Remix by Michael Kubina http://www.kubina.info Original by: https://forum.fritzing.org/t/current-sensor-5a-acs712/7694 https://forum.fritzing.org/u/ArtHome ArtHome12@gmail.com
  Module display OLED I2C 128x64 SSD1306: Ecran OLED I2C SSD163 de 128x64 avec connexion I2C
  TP4056: A DIP stand-in part for whatever IC you want. With 6 pins on a 300mil dual inline package (DIP) footprint.
